# Fritzing sketch platine_breadboard_only (saved by Fritzing 0.9.10b)
stripboards: 1

parts:
  Bauteil1 = Arduino Nano (Rev3.0)
  LCD1 = LCD screen
  R1 = Trimmer Potentiometer [maximum_resistance=10kΩ knob_status=50% power=0.5W package=THT]
  R2 = Resistor [tolerance=±5% power=0.25 resistance=560 package=THT]
  RE1 = KY-040 Rotary encoder [package=THT]
  microSD1 = MicroSD Card Module
  S1 = Round Pushbutton
  S2 = Round Pushbutton
  S3 = Round Pushbutton
  R3 = Resistor [tolerance=±5% power=0.25 resistance=10k package=THT]
  R4 = Resistor [tolerance=±5% power=0.25 resistance=10k package=THT]
  R5 = Resistor [tolerance=±5% power=0.25 resistance=10k package=THT]
  Power_plug1 = Power plug

nets:
  GND: Bauteil1.GND, LCD1.VSS, LCD1.R/W, LCD1.LED-, R1.leg1, RE1.GND, microSD1.GND, R3.Pin_1, R4.Pin_1, R5.Pin_1, Power_plug1.GND
  N1: Bauteil1.D2, RE1.SW
  N2: Bauteil1.D3, RE1.DT
  N3: Bauteil1.D4, RE1.CLK
  N4: Bauteil1.D5, S3.leg0, R3.Pin_0
  N5: Bauteil1.D6, S2.leg0, R5.Pin_0
  N6: Bauteil1.D7, S1.leg0, R4.Pin_0
  N7: Bauteil1.D10, microSD1.CS
  N8: Bauteil1.D11/MOSI, microSD1.MOSI
  N9: Bauteil1.D12/MISO, microSD1.MISO
  VIN: Bauteil1.VIN, Power_plug1.VCC
  VCC: Bauteil1.5V, LCD1.VDD, R1.leg2, RE1.Vcc, microSD1.VCC, S1.leg1, S2.leg1
  N10: Bauteil1.A7, LCD1.RS
  N11: Bauteil1.A6, LCD1.E
  N12: Bauteil1.A5, LCD1.DB4
  N13: Bauteil1.A4, LCD1.DB5
  N14: Bauteil1.A3, LCD1.DB6
  N15: Bauteil1.A2, LCD1.DB7
  N16: Bauteil1.A1, R2.Pin_0
  N17: Bauteil1.D13/SCK, microSD1.SCK
  N18: LCD1.V0, R1.wiper
  N19: LCD1.LED+, R2.Pin_1

custom parts:
  KY-040 Rotary encoder: KY-040 Rotary Encoder with switch on breakout borad from AZ Delivery
